// Logisim project mips.circ as structural Verilog: 6 circuits, main circuit main
module main (
);

  wire clock_1_out, uc_1_reg_dest, uc_1_reg_op, uc_1_reg_write, uc_1_ula_src;
  wire [4:0] multiplexer_1_out;
  wire [5:0] ula_control_1_out_3;
  wire [6:0] uc_1_out_6;
  wire [23:0] adder_1_out, register_1_q;
  wire [31:0] bit_extender_1_out, br_1_br_rs, br_1_br_rs_2, multiplexer_2_out, multiplexer_3_out, ram_1_data,
       ram_2_data, ula_1_out_4;

  Adder #(.width(24)) adder_1 (.a(register_1_q), .b(24'h1), .out(adder_1_out));  // open: cin, cout
  Register #(.width(24), .Select("low")) register_1 (
    .D(adder_1_out), .Q(register_1_q), .clk(clock_1_out));  // open: en, clr
  Clock clock_1 (.out(clock_1_out));
  RAM #(.addrWidth(24), .dataWidth(32), .Select("low")) ram_1 (
    .addr(register_1_q), .data(ram_1_data), .clk(clock_1_out));  // open: sel, ld, clr
  UC uc_1 (
    .in_1(ram_1_data[31:26]), .reg_write(uc_1_reg_write), .reg_dest(uc_1_reg_dest), .reg_op(uc_1_reg_op),
    .ula_src(uc_1_ula_src), .out_6(uc_1_out_6));
  Multiplexer #(.width(5), .enable("false")) multiplexer_1 (
    .in0(ram_1_data[20:16]), .in1(ram_1_data[15:11]), .out(multiplexer_1_out), .sel(uc_1_reg_dest));
  assign bit_extender_1_out = {{16{1'b0}}, ram_1_data[15:0]};  // Bit_Extender bit_extender_1
  ula_control ula_control_1 (.funct(ram_1_data[5:0]), .uc_op(uc_1_out_6), .out_3(ula_control_1_out_3));
  BR br_1 (
    .rs(ram_1_data[25:21]), .rt(ram_1_data[20:16]), .rd(multiplexer_1_out), .BR_RS(br_1_br_rs),
    .BR_RS_2(br_1_br_rs_2), .reg_write(uc_1_reg_write), .clk(clock_1_out), .data(multiplexer_3_out));
  Multiplexer #(.width(32), .enable("false")) multiplexer_2 (
    .in0(br_1_br_rs_2), .in1(bit_extender_1_out), .out(multiplexer_2_out), .sel(uc_1_ula_src));
  Multiplexer #(.width(32), .enable("false")) multiplexer_3 (
    .in0(ula_1_out_4), .in1(ram_2_data), .out(multiplexer_3_out), .sel(uc_1_reg_op));
  ULA ula_1 (.in_1(br_1_br_rs), .in_2(multiplexer_2_out), .out_4(ula_1_out_4), .in_3(ula_control_1_out_3));
  RAM #(.addrWidth(24), .dataWidth(32), .Select("low")) ram_2 (
    .addr(ula_1_out_4[23:0]), .data(ram_2_data));  // open: sel, clk, ld, clr
endmodule

module BR (
  input  reg_write,
  input  [4:0] rs,
  input  [4:0] rt,
  input  [4:0] rd,
  input  [31:0] data,
  input  clk,
  output [31:0] BR_RS,
  output [31:0] BR_RS_2
);

  wire demultiplexer_1_out0, demultiplexer_1_out1, demultiplexer_1_out2, undriven;
  wire [31:0] register_1_q, register_2_q, register_4_q, register_5_q, register_10_q;

  Demultiplexer #(.select(2), .enable("false")) demultiplexer_1 (
    .out0(demultiplexer_1_out0), .out1(demultiplexer_1_out1), .out2(demultiplexer_1_out2), .in(reg_write),
    .sel(rd[1:0]));  // open: out3
  Register #(.width(32), .Select("low")) register_1 (.D(data), .Q(register_1_q), .clk(clk));  // open: en, clr
  Register #(.width(32), .Select("low")) register_2 (.D(data), .Q(register_2_q), .clk(clk));  // open: en, clr
  Register #(.width(32), .Select("low")) register_3 (.clk(undriven));  // open: D, en, Q, clr
  Register #(.width(32), .Select("low")) register_4 (
    .D(data), .en(demultiplexer_1_out2), .Q(register_4_q), .clk(clk));  // open: clr
  Register #(.width(32), .Select("low")) register_5 (
    .D(data), .en(demultiplexer_1_out1), .Q(register_5_q), .clk(clk));  // open: clr
  Register #(.width(32), .Select("low")) register_6 (.clk(clk));  // open: D, en, Q, clr
  Register #(.width(32), .Select("low")) register_7 (.clk(clk));  // open: D, en, Q, clr
  Register #(.width(32), .Select("low")) register_8 ();  // open: D, en, Q, clk, clr
  Register #(.width(32), .Select("low")) register_9 ();  // open: D, en, Q, clk, clr
  Register #(.width(32), .Select("low")) register_10 (.D(data), .Q(register_10_q), .clk(clk));  // open: en, clr
  Register #(.width(32), .Select("low")) register_11 (.clk(clk));  // open: D, en, Q, clr
  Register #(.width(32), .Select("low")) register_12 ();  // open: D, en, Q, clk, clr
  Multiplexer #(.select(3), .width(32), .enable("false")) multiplexer_1 (
    .in0(register_1_q), .in1(register_5_q), .in2(register_4_q), .in3(register_10_q), .in4(register_2_q),
    .out(BR_RS), .sel(rs[2:0]));  // open: in5, in6, in7
  Multiplexer #(.select(3), .width(32), .enable("false")) multiplexer_2 (
    .in0(register_1_q), .in1(register_5_q), .in2(register_4_q), .in3(register_10_q), .in4(register_2_q),
    .out(BR_RS_2), .sel(rt[2:0]));  // open: in5, in6, in7
endmodule

module ULA (
  input  [31:0] in_1,
  input  [31:0] in_2,
  input  [5:0] in_3,
  output [31:0] out_4
);

  wire adder_1_cout, subtractor_1_bout;
  wire [31:0] adder_1_out, divider_1_out, divider_1_rem, multiplier_1_cout, multiplier_1_out,
       subtractor_1_out;

  Adder #(.width(32)) adder_1 (.a(in_1), .b(in_2), .out(adder_1_out), .cout(adder_1_cout));  // open: cin
  Subtractor #(.width(32)) subtractor_1 (
    .a(in_1), .b(in_2), .out(subtractor_1_out), .bout(subtractor_1_bout));  // open: bin
  Multiplier #(.width(32)) multiplier_1 (
    .a(in_1), .b(in_2), .out(multiplier_1_out), .cout(multiplier_1_cout));  // open: cin
  Divider #(.width(32)) divider_1 (.a(in_1), .b(in_2), .out(divider_1_out), .rem(divider_1_rem));  // open: upper
  Multiplexer #(.select(2), .width(32), .enable("false")) multiplexer_1 (
    .in0(adder_1_out), .in1(subtractor_1_out), .in2(multiplier_1_out), .in3(divider_1_out), .out(out_4),
    .sel(in_3[1:0]));
endmodule

module UC (
  input  [5:0] in_1,
  output reg_write,
  output reg_dest,
  output reg_op,
  output ula_src,
  output [6:0] out_6
);

  UC_IN uc_in_1 (
    .a(in_1[0]), .b(in_1[1]), .c(in_1[2]), .d(in_1[3]), .e(in_1[4]), .f(in_1[5]), .reg_write(reg_write),
    .reg_dest(reg_dest), .reg_op(reg_op), .ula_src(ula_src), .uc_op6(out_6[6]), .uc_op5(out_6[5]),
    .uc_op4(out_6[4]), .uc_op3(out_6[3]), .uc_op2(out_6[2]), .uc_op1(out_6[1]), .uc_op0(out_6[0]));
endmodule

module UC_IN (
  input  a,
  input  b,
  input  c,
  input  d,
  input  e,
  input  f,
  output reg_write,
  output reg_dest,
  output reg_op,
  output ula_src,
  output uc_op6,
  output uc_op5,
  output uc_op4,
  output uc_op3,
  output uc_op2,
  output uc_op1,
  output uc_op0
);

  wire not_1_out;

  not not_1 (not_1_out, f);
  not not_2 (reg_dest, d);
  or or_1 (reg_write, not_1_out, e, d, c, b, a);

  assign reg_op = e;
  assign uc_op0 = e;
  assign uc_op1 = 1'b0;
  assign uc_op2 = 1'b0;
  assign uc_op3 = 1'b0;
  assign uc_op4 = 1'b0;
  assign uc_op5 = 1'b0;
  assign uc_op6 = 1'b0;
  assign ula_src = e;
endmodule

module ula_control (
  input  [5:0] funct,
  input  [6:0] uc_op,
  output [5:0] out_3
);

  Multiplexer #(.width(6), .enable("false")) multiplexer_1 (.in0(funct), .in1(uc_op[6:1]), .out(out_3), .sel(uc_op[0]));
endmodule
